# Fritzing sketch motor293D (saved by Fritzing 0.8.3b)
breadboards: 1

parts:
  Part1 = Arduino Uno (Rev3)
  IC1 = L293D [package=THT]
  M1 = DC Motor
  M2 = DC Motor
  BAT1 = BC9VPC [package=bc9vpc]

nets:
  N1: Part1.GND, IC1.0V, BAT1.V+
  N2: Part1.D9_PWM, IC1.In_2
  N3: Part1.D3_PWM, IC1.In_3
  N4: Part1.D5_PWM, IC1.In_4
  N5: Part1.D6_PWM, IC1.In_1
  N6: Part1.5V, IC1.Enable_1, IC1.+Vmotor, IC1.Enable_2
  N7: Part1.VIN, IC1.+V, BAT1.V-
  N8: IC1.Out_1_(_Controlled_by_Enable_1_), M2.pin_2
  N9: IC1.Out_2_(_Controlled_by_Enable_1_), M2.pin_1
  N10: IC1.Out_3_(_Controlled_by_Enable_2_), M1.pin_2
  N11: IC1.Out_4_(_Controlled_by_Enable_2_), M1.pin_1

notes:
  Notch on 293D is to the right
